# Fritzing sketch GeminiPrj (saved by Fritzing 0.9.5d)

parts:
  Mod1 = Raspberry Pi 4B
  S1 = H-Bridge with L298N
  M1 = DC Motor
  M2 = DC Motor
  M3 = DC Motor
  M4 = DC Motor
  BAT1 = 12 battery [package=battery]
  U1 = SWITCH-SPST-2 [package=switch-spst-vertical]
  M5 = RioRand LM2596

nets:
  GND: Mod1.GND, S1.GND, BAT1.-, M5.Pin_2, M5.Pin_4
  N1: Mod1.GPIO17, S1.ENA
  N2: Mod1.GPIO18, S1.ENB
  N3: Mod1.GPIO27, S1.IN1
  N4: Mod1.GPIO22, S1.IN2
  N5: Mod1.GPIO23, S1.IN3
  N6: Mod1.GPIO24, S1.IN4
  N7: S1.12V, M5.Pin_1
  N8: S1.5V, M5.Pin_3
  N9: S1.M1-01, M2.pin_2, M3.pin_2
  N10: S1.M1-02, M2.pin_1, M3.pin_1
  N11: S1.M2-01, M1.pin_2, M4.pin_2
  N12: S1.M2-02, M1.pin_1, M4.pin_1
  N13: BAT1.+, U1.P

notes:
  Right
  Left

custom parts:
  H-Bridge with L298N: h-bridge
  12 battery: 12V lead acid type battery, like the Husqvarna YTH2448 12V 35AH battery. This is the mini version 1/4 the size of the actual battery to be closer to typical breadboard parts (around 2in wide rathher than 7in). The pads in pcb are sized to accomidate up to 14ga wire (as these batterys will deliver high currents.)
